# Fritzing sketch Final_Setup (saved by Fritzing 1.0.4)
circuit board: 8.46667cm x 5.64444cm
breadboards: 1

parts:
  Part1 = Arduino Pro Mini (3.3V)
  J1 = Piezo Speaker
  BAT1 = Battery Holders [package=battery-aa]
  IR1 = TSOP312.., 314.. [package=THT]
  D1 = LTE-302 [package=lte-302]
  INA1 = INA219 DC Current Sensor Breakout
  A1 = FT232-AZ USB to TTL serial adapter
  Part2 = NCP1400 Step-Up Breakout
  C1 = Capacitor [package=cap-pth-small2]
  LCM1602_IIC1 = LCM1602 IIC [part_number="LCM1602 IIC" chip_label="LCM1602 IIC" package="DIP (Dual Inline) [THT]"]
  U1 = LCD-16X2 [package=lcd-16x2_noholes]
  ZS-042_RTC1 = ZS-042 RTC Module
  microSD1 = MicroSD Card Module
  S1 = Pushbutton [package="[THT]"]
  R1 = Resistor [tolerance=±5% resistance=100k package="1206 [SMD]"]
  S2 = SWITCH-SPST-2 [package=switch-spst-vertical]

nets (from the breadboard view):
  N1: Part1.TXO, A1.Pin_8, A1.Pin_12, A1.Pin_19
  N2: Part1.RXI, A1.Pin_7, A1.Pin_11, A1.Pin_23
  VCC: Part1.VCC, IR1.Vs, INA1.VCC, Part2.VOUT, LCM1602_IIC1.VCC, ZS-042_RTC1.VCC, microSD1.VCC, R1.Pin_0
  GND: Part1.GND, Part1.D5, J1.pin1, BAT1.+, IR1.GND, D1.C, INA1.GND, A1.Pin_9, A1.Pin_15, Part2.GND, LCM1602_IIC1.GND, ZS-042_RTC1.GND, microSD1.GND, S1.Pin_3, S1.Pin_4, R1.Pin_1
  N3: Part1.A4, INA1.SDA, LCM1602_IIC1.SDA, ZS-042_RTC1.SDA
  N4: Part1.A5, INA1.SCL, LCM1602_IIC1.SCL, ZS-042_RTC1.SCL
  N5: Part1.RESET, C1.2
  N6: Part1.SCK, microSD1.SCK
  N7: Part1.MISO, microSD1.MISO
  N8: Part1.MOSI, microSD1.MOSI
  N9: Part1.D10, microSD1.CS
  N10: Part1.D4, IR1.Data
  N11: Part1.D3, D1.A
  N12: Part1.D2, J1.pin2
  N13: BAT1.-, INA1.Vin+, S2.O, S2.P
  N14: INA1.Vin-, Part2.VIN
  N15: A1.Pin_10, C1.1
  N16: A1.Pin_17, A1.Pin_18
  VSS: LCM1602_IIC1.VSS, U1.VSS
  VDD: LCM1602_IIC1.VDD, U1.VDD
  N17: LCM1602_IIC1.V0, U1.VO
  N18: LCM1602_IIC1.RS, U1.RS
  N19: LCM1602_IIC1.RW, U1.R_W
  N20: LCM1602_IIC1.E, U1.E
  N21: LCM1602_IIC1.D0, U1.DB0
  N22: LCM1602_IIC1.D1, U1.DB1
  N23: LCM1602_IIC1.D2, U1.DB2
  N24: LCM1602_IIC1.D3, U1.DB3
  N25: LCM1602_IIC1.D4, U1.DB4
  N26: LCM1602_IIC1.D5, U1.DB5
  N27: LCM1602_IIC1.D6, U1.DB6
  N28: LCM1602_IIC1.D7, U1.DB7
  N29: LCM1602_IIC1.A, U1.A
  N30: LCM1602_IIC1.K, U1.K
  N31: LCM1602_IIC1.LED_A, LCM1602_IIC1.LED_B
  N32: S1.Pin_1, S1.Pin_2

custom parts:
  INA219 DC Current Sensor Breakout: INA DC Current Sensor Breakout
  FT232-AZ USB to TTL serial adapter: FT232-AZ USB to TTL serial adapter.
  LCM1602 IIC: I2C-Module to use a 1602 or 2004 LCD on with the wire.h libory Serial LCD Modul
